# Fritzing sketch Dmxuino-01 (saved by Fritzing 0.8.5b)
breadboards: 1

parts:
  U1 = MAX485 [package=dil08]
  XLRout = XLR3_NCFAH2 [package=xlr3_nc3fah2]  # not connected
  µP = Arduino Uno (Rev3) - ICSP
  C1 = Ceramic Capacitor [capacitance=1µF package="100 mil [THT, multilayer]"]

nets:
  N1: U1.DI, µP.D1/TX
  GND: U1.GND, µP.GND, C1.0
  VCC: U1.VCC, µP.5V, C1.1
